# Fritzing sketch mqtt-ds18b20 (saved by Fritzing 0.9.1b)
circuit board: 6.23147cm x 3.95791cm
breadboards: 1

parts:
  U1 = ESP8266 WiFi Module [part_number=ESP8266]
  JP3 = Header 4 [package=molex-1x4_lock]
  S1 = Momentary Switch [package=tactile-pth]
  R1 = Resistor [tolerance=±5% resistance=4.7k package=THT]
  C1 = Capacitor Polarized [package=cpol-radial-100uf-25v]
  T1 = LM35 Temperature Sensor [package="TO92 [THT]"]
  IC1 = Voltage Regulator LM1117 [package=sot223]
  RHT1 = Humidity and Temperature Sensor RHT03
  R2 = Resistor [tolerance=±5% resistance=220 package=THT]
  J1 = Screw terminal - 2 pins [package=THT]
  J2 = Screw terminal - 2 pins [package=THT]

nets:
  N1: U1.RXD, JP3.3
  VCC: U1.VCC, U1.CH_PD, JP3.4, R1.Pin_1, C1.+, IC1.OUT, RHT1.Vcc, R2.Pin_1
  N2: U1.GPIO_0, S1.1, RHT1.Data-signal, R2.Pin_0
  N3: U1.GPIO_2, R1.Pin_0, T1.Vout, J2.pin2
  GND: U1.GND, JP3.1, S1.4, C1.-, T1.GND, IC1.ADJ, RHT1.GND_2, J1.pin2, J2.pin1
  N4: U1.TXD, JP3.2
  N5: IC1.IN, J1.pin1

notes:
  GND
  VCC
  (3.3v)
  Rx
  Tx
  (4-7v)
  1-wire
  data
  Huelvayork - 2015-04
  DHT11/22
  ds18b20
  4.7K
  1K

custom parts:
  ESP8266 WiFi Module: Generic WiFi Module based on the ESP8266 with onboard PCB antenna and UART communications
